# Fritzing sketch rfm69_TEENSY (saved by Fritzing 0.9.10b)
breadboards: 1

parts:
  Teensy1 = Teensy 4.1
  Part3 = Adafruit RFM9x LoRa Radio [part_number="Adafruit #3072 and #3073"]

nets:
  N1: Teensy1.GND, Teensy1.GND2#55
  N2: Teensy1.D3, Part3.DIO0
  N3: Teensy1.D9, Part3.RST
  N4: Teensy1.D10, Part3.CS
  N5: Teensy1.D11, Part3.MOSI
  N6: Teensy1.D12, Part3.MISO
  N7: Teensy1.D13, Part3.SCK
  N8: Teensy1.3V3_LOW, Part3.VIN
  N9: Teensy1.GND2#31, Part3.GND

notes:
  Teensy is 3V logic level, connect radio power to 3V pin!
  Connect radio to SPI pins and as described in code

custom parts:
  Teensy 4.1: The Teensy is a complete USB-based microcontoller development system, in a very small footprint, capable of implementing many types of projects. All programming is done via the USB port. No special programmer is needed, only a standard micro-USB cable and a PC or Macintosh with a USB port.
  Adafruit RFM9x LoRa Radio: Sending data over long distances is like magic, and now you can be a magician with this range of powerful and easy-to-use radio modules. Sure, sometimes you want to talk to a computer (a good time to use WiFi) or perhaps communicate with a Phone (choose Bluetooth Low Energy!) but what if you want to send data very far? Most WiFi, Bluetooth, Zigbee and other wireless chipsets use 2.4GHz, which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
